# Fritzing sketch Prototype (saved by Fritzing 0.8.0b)
breadboards: 6

parts:
  Part1 = Arduino Mega 2560 (Rev3)
  Part2 = Barometric Pressure Sensor - BMP085 Breakout
  R1 = Resistor [tolerance=±5% resistance=220 package=THT]
  TMP1 = TMP006 Temperature Sensor
  GPS1 = Adafruit Ultimate GPS Breakout
  DHT1 = DHT11 Humitidy and Temperature Sensor
  Part3 = Serial Alphanumeric Display Driver  # not connected
  S1 = Tilt Switch [package=THT]
  ADXL1 = ADXL335 Accelerometer Breakout
  microSD1 = MicroSD Breakout

nets:
  N1: Part1.A8, ADXL1.Yout
  N2: Part1.A9, ADXL1.Xout
  N3: Part1.A10, ADXL1.GND
  N4: Part1.D21/SCL, TMP1.DRDY
  N5: Part1.D20/SDA, TMP1.AD1
  N6: Part1.D15/RX3, GPS1.RX
  N7: Part1.D14/TX3, GPS1.GND
  3V3: Part1.3V3, TMP1.AD0, ADXL1.Vin
  5V: Part1.5V, Part2.VCC, R1.Pin_0, GPS1.PPS, DHT1.VDD, S1.Pin_1, microSD1.5V
  GND: Part1.GND, Part1.D35, Part2.GND, TMP1.GND, GPS1.VIN, DHT1.NULL, S1.Pin_2, ADXL1.3Vo, microSD1.GND
  N8: Part1.D7_PWM, Part2.SDA
  N9: Part1.D24, R1.Pin_1, DHT1.DATA
  N10: Part1.D48, Part2.SCL
  N11: Part1.D49, Part2.XCLR
  N12: Part1.D50, Part2.EOC

custom parts:
  TMP006 Temperature Sensor: TMP006 Contact-less Infrared Thermopile Sensor Breakout
  DHT11 Humitidy and Temperature Sensor: DHT11 Humidity and Temperature Sensor
  ADXL335 Accelerometer Breakout: ADXL335 Accelerometer Breakout board
  MicroSD Breakout: 5V-ready microSD Breakout with Level Shifter
