# Fritzing sketch Weather Balloon (saved by Fritzing 0.8.0b)
breadboards: 2
perfboards: 1

parts:
  Part1 = Arduino Mega 2560 (Rev3)
  Part2 = Arduino MicroSD Shield
  DHT1 = DHT11 Humitidy and Temperature Sensor
  ADXL1 = ADXL335 Accelerometer Breakout
  Geiger_Counter = Serial Alphanumeric Display Driver  # not connected
  R1 = Resistor [tolerance=±5% resistance=220 package=THT]
  R2 = Resistor [tolerance=±5% resistance=220 package=THT]
  Part3 = Gas Sensor Breakout Board
  Part4 = Barometric Pressure Sensor - BMP085 Breakout  # not connected
  FLORA1 = Adafruit_Flora
  Part5 = _TL2561

nets:
  N1: Part1.A8, ADXL1.Zout
  N2: Part1.A9, ADXL1.Yout
  N3: Part1.A10, ADXL1.Xout
  N4: Part1.A14, Part3.B1
  N5: Part1.D19/RX1, FLORA1.connector6
  N6: Part1.D18/TX1, FLORA1.connector5
  N7: Part1.D22, DHT1.DATA, R1.Pin_1
  5V: Part2.5V, Part2.3.3V, DHT1.VDD, ADXL1.3Vo, R1.Pin_0, Part3.B2, FLORA1.connector4, Part5.Vcc
  GND: Part2.GND, ADXL1.GND, R2.Pin_1, Part3.GND, FLORA1.connector7, Part5.GND
  N8: R2.Pin_0, Part3.A2

notes:
  We used an MPL115A1

custom parts:
  DHT11 Humitidy and Temperature Sensor: DHT11 Humidity and Temperature Sensor
  ADXL335 Accelerometer Breakout: ADXL335 Accelerometer Breakout board
  : Sensor de Luminosidade - TL2561
